// Logisim project BITWISEAND.circ as structural Verilog: 1 circuit, main circuit BITWISEAND
module BITWISEAND (
  input  A7,
  input  A6,
  input  A5,
  input  A4,
  input  A3,
  input  A2,
  input  A1,
  input  A0,
  input  B7,
  input  B6,
  input  B5,
  input  B4,
  input  B3,
  input  B2,
  input  B1,
  input  B0,
  output O7,
  output O6,
  output O5,
  output O4,
  output O3,
  output O2,
  output O1,
  output O0
);

  and _7 (O7, A7, B7);
  and _6 (O6, A6, B6);
  and _5 (O5, A2, B5);
  buf _4 (O4, B4);  // AND_Gate
  buf _3 (O3, A3);  // AND_Gate
  buf _2 (O2, A2);  // AND_Gate
  buf _1 (O1, B1);  // AND_Gate
  and _0 (O0, B0, B2);

  assign A5 = A2;
endmodule
