// Logisim project BITWISEFUNCTIONS.circ as structural Verilog: 1 circuit, main circuit main
module main (
  input  A7,
  input  A6,
  input  A5,
  input  A4,
  input  A3,
  input  A2,
  input  A1,
  input  A0,
  input  B7,
  input  B6,
  input  B5,
  input  B4,
  input  B3,
  input  B2,
  input  B1,
  input  B0,
  input  A7_2,
  input  A6_2,
  input  A5_2,
  input  A4_2,
  input  A3_2,
  input  A2_2,
  input  A1_2,
  input  A0_2,
  input  B7_2,
  input  B6_2,
  input  B5_2,
  input  B4_2,
  input  B3_2,
  input  B2_2,
  input  B1_2,
  input  B0_2,
  input  A0_3,
  input  A6_3,
  input  A5_3,
  input  A4_3,
  input  A3_3,
  input  A2_3,
  input  A1_3,
  input  A0_4,
  output O7,
  output O6,
  output O5,
  output O4,
  output O3,
  output O2,
  output O1,
  output O0,
  output _7,
  output _6,
  output _5,
  output _4,
  output _3,
  output _2,
  output _1,
  output _0,
  output _7_2,
  output _6_2,
  output _5_2,
  output _4_2,
  output _3_2,
  output _2_2,
  output _1_2,
  output _0_2
);

  not u__7 (_7_2, A0_3);
  not u__6 (_6_2, A6_3);
  not u__5 (_5_2, A5_3);
  not u__4 (_4_2, A4_3);
  not u__3 (_3_2, A3_3);
  not u__2 (_2_2, A2_3);
  not u__1 (_1_2, A1_3);
  not u__0 (_0_2, A0_4);
  or u__7_2 (_7, A7_2, B7_2);
  or u__6_2 (_6, A6_2, B6_2);
  or u__5_2 (_5, A3_2, B5_2);
  or u__4_2 (_4, A4_2, B4_2);
  or u__3_2 (_3, A3_2, B3_2);
  or u__2_2 (_2, A2_2, B2_2);
  or u__1_2 (_1, A1_2, B1_2);
  or u__0_2 (_0, A0_2, B0_2);
  and _7_3 (O7, A7, B7);
  and _6_3 (O6, A6, B6);
  and _5_3 (O5, A2, B5);
  buf _4_3 (O4, B4);  // AND_Gate
  buf _3_3 (O3, A3);  // AND_Gate
  buf _2_3 (O2, A2);  // AND_Gate
  buf _1_3 (O1, B1);  // AND_Gate
  and _0_3 (O0, B0, B2);

  assign A5 = A2;
  assign A5_2 = A3_2;
endmodule
