// Logisim project BITWISENOT.circ as structural Verilog: 1 circuit, main circuit main
module main (
  input  A7,
  input  A6,
  input  A5,
  input  A4,
  input  A3,
  input  A2,
  input  A1,
  input  A0,
  output _7,
  output _6,
  output _5,
  output _4,
  output _3,
  output _2,
  output _1,
  output _0
);

  not u__7 (_7, A7);
  not u__6 (_6, A6);
  not u__5 (_5, A5);
  not u__4 (_4, A4);
  not u__3 (_3, A3);
  not u__2 (_2, A2);
  not u__1 (_1, A1);
  not u__0 (_0, A0);
endmodule
