// Logisim project BITWISEOR.circ as structural Verilog: 1 circuit, main circuit main
module main (
  input  A7,
  input  A6,
  input  A5,
  input  A4,
  input  A3,
  input  A2,
  input  A1,
  input  A0,
  input  B7,
  input  B6,
  input  B5,
  input  B4,
  input  B3,
  input  B2,
  input  B1,
  input  B0,
  output _7,
  output _6,
  output _5,
  output _4,
  output _3,
  output _2,
  output _1,
  output _0
);

  or u__7 (_7, A7, B7);
  or u__6 (_6, A6, B6);
  or u__5 (_5, A3, B5);
  or u__4 (_4, A4, B4);
  or u__3 (_3, A3, B3);
  or u__2 (_2, A2, B2);
  or u__1 (_1, A1, B1);
  or u__0 (_0, A0, B0);

  assign A5 = A3;
endmodule
