// Logisim project AdderCircutis.circ as structural Verilog
module halfAdder (
  input  A,
  input  B,
  output S,
  output C
);

  or or_1 (S, A, B);
  and and_1 (C, A, B);
endmodule

module fullAdder (
  input  B,
  input  A,
  input  Cin,
  output S,
  output Cout
);

  wire and_1_out, and_2_out, or_1_out;

  or or_1 (or_1_out, A, B);
  and and_1 (and_1_out, or_1_out, Cin);
  and and_2 (and_2_out, A, B);
  or or_2 (S, or_1_out, Cin);
  or or_3 (Cout, and_1_out, and_2_out);
endmodule

module _8bitRippleCarryAdder (
  input  B7,
  input  A7,
  input  B6,
  input  A6,
  input  B5,
  input  A5,
  input  B4,
  input  A4,
  input  B3,
  input  A3,
  input  B2,
  input  A2,
  input  B1,
  input  A1,
  input  B0,
  input  A0,
  input  CIN,
  output COUT,
  output S7,
  output S6,
  output S5,
  output S4,
  output S3,
  output S2,
  output S1,
  output S0
);

  wire fulladder_2_cout, fulladder_3_cout, fulladder_4_cout, fulladder_5_cout, fulladder_6_cout,
       fulladder_7_cout, fulladder_8_cout;

  fullAdder fulladder_1 (.Cout(COUT), .B(B7), .A(A7), .S(S7), .Cin(fulladder_2_cout));
  fullAdder fulladder_2 (.Cout(fulladder_2_cout), .B(B6), .A(A6), .S(S6), .Cin(fulladder_3_cout));
  fullAdder fulladder_3 (.Cout(fulladder_3_cout), .B(B5), .A(A5), .S(S5), .Cin(fulladder_4_cout));
  fullAdder fulladder_4 (.Cout(fulladder_4_cout), .B(B4), .A(A4), .S(S4), .Cin(fulladder_5_cout));
  fullAdder fulladder_5 (.Cout(fulladder_5_cout), .B(B3), .A(A3), .S(S3), .Cin(fulladder_6_cout));
  fullAdder fulladder_6 (.Cout(fulladder_6_cout), .B(B2), .A(A2), .S(S2), .Cin(fulladder_7_cout));
  fullAdder fulladder_7 (.Cout(fulladder_7_cout), .B(B1), .A(A1), .S(S1), .Cin(fulladder_8_cout));
  fullAdder fulladder_8 (.Cout(fulladder_8_cout), .B(B0), .A(A0), .S(S0), .Cin(CIN));
endmodule
